// Logisim project trab.circ as structural Verilog: 3 circuits, main circuit main
module main (
);

  wire and_1_out, button_1_out, CLK, CONTROL_UNIT_p2, CONTROL_UNIT_p3, CONTROL_UNIT_p4, CONTROL_UNIT_p8, HLT,
       not_1_out, not_2_out, not_3_out, STR;
  wire [1:0] RAMADDR;
  wire [4:0] counter_1_q;
  wire [7:0] ram_1_data, RAMIN, RAMOUT, rom_1_data;

  Clock clock_1 (.out(CLK));
  Counter #(.width(5), .max('h1f)) counter_1 (
    .Q(counter_1_q), .clk(and_1_out), .clr(button_1_out));  // open: load, D, count, carry
  and and_1 (and_1_out, not_1_out, CLK);
  not not_1 (not_1_out, HLT);
  not not_2 (not_2_out, STR);
  Button button_1 (.out(button_1_out));
  RAM #(.addrWidth(2), .bus("asynch")) ram_1 (.addr(RAMADDR), .data(ram_1_data), .ld(not_2_out));  // open: sel, clr
  not not_3 (not_3_out, STR);
  assign RAMOUT = not_3_out ? ram_1_data : 8'bz;  // Controlled_Buffer controlled_buffer_1
  assign ram_1_data = STR ? RAMIN : 8'bz;  // Controlled_Buffer controlled_buffer_2
  ROM #(.addrWidth(5)) rom_1 (.addr(counter_1_q), .data(rom_1_data));  // open: sel
  assign RAMOUT = STR ? {8{1'b0}} : 8'bz;  // Controlled_Buffer controlled_buffer_3
  Register INSTRUCTION_REGISTER (.D(rom_1_data), .clk(CLK));  // open: en, Q, clr
  // CONTROL_UNIT CONTROL_UNIT: pin names not known; wires that end beside it: rom_1_data, CONTROL_UNIT_p2, CONTROL_UNIT_p3, CONTROL_UNIT_p4, RAMADDR, STR, HLT, CONTROL_UNIT_p8
  // ALU ALU: pin names not known; wires that end beside it: CONTROL_UNIT_p2, STR, CONTROL_UNIT_p8, CONTROL_UNIT_p3, CONTROL_UNIT_p4, RAMOUT, CLK, RAMIN

  // Notes on the sheet:
  //   RAM
  //   ROM
  //   contents of rom_1 (hex, n*v repeats v):
  //   d0 d5 da df e3 e6 e9 ec 0 84
endmodule

module CONTROL_UNIT (
  input  [7:0] INSTR,
  output RDM,
  output [1:0] REGADDR0,
  output [1:0] REGADDR1,
  output [1:0] RAMADDR,
  output STR,
  output HLT,
  output ADD
);

  wire and_1_out, and_2_out, and_3_out, and_4_out, and_5_out, and_6_out, and_7_out, and_8_out, not_1_out,
       not_2_out, not_3_out, not_4_out, not_5_out, not_6_out, not_7_out;

  and and_1 (and_1_out, INSTR[7], INSTR[6]);
  and and_2 (and_2_out, INSTR[7], INSTR[6]);
  and and_3 (and_3_out, INSTR[7], not_1_out);
  not not_1 (not_1_out, INSTR[6]);
  and and_4 (and_4_out, INSTR[7], not_2_out);
  not not_2 (not_2_out, INSTR[6]);
  not not_3 (not_3_out, INSTR[5]);
  and and_5 (and_5_out, and_2_out, INSTR[5]);
  and and_6 (and_6_out, and_3_out, not_4_out);
  not not_4 (not_4_out, INSTR[5]);
  and and_7 (and_7_out, and_4_out, not_5_out);
  not not_5 (not_5_out, INSTR[5]);
  and and_8 (and_8_out, and_1_out, not_3_out);
  and and_9 (RDM, and_8_out, INSTR[4]);
  and and_10 (STR, and_5_out, not_6_out);
  not not_6 (not_6_out, INSTR[4]);
  and and_11 (HLT, and_6_out, not_7_out);
  not not_7 (not_7_out, INSTR[4]);
  and and_12 (ADD, and_7_out, INSTR[4]);
  assign REGADDR1 = ADD ? INSTR[1:0] : 2'bz;  // Controlled_Buffer controlled_buffer_1
  assign REGADDR0 = STR ? INSTR[3:2] : 2'bz;  // Controlled_Buffer controlled_buffer_2
  assign REGADDR0 = RDM ? INSTR[3:2] : 2'bz;  // Controlled_Buffer controlled_buffer_3
  assign RAMADDR = STR ? INSTR[1:0] : 2'bz;  // Controlled_Buffer controlled_buffer_4
  assign RAMADDR = RDM ? INSTR[1:0] : 2'bz;  // Controlled_Buffer controlled_buffer_5
endmodule

module ALU (
  input  RDM,
  input  STR,
  input  ADD,
  input  CLK,
  input  [7:0] RAMOUT,
  input  [1:0] REGADRR0,
  input  [1:0] REGADRR1,
  output [7:0] REGOUT
);

  wire and_1_out, and_2_out, and_3_out, and_4_out, and_5_out, and_6_out, and_7_out, and_8_out, and_9_out,
       and_10_out, and_11_out, and_12_out, and_13_out, and_14_out, not_1_out, not_2_out, not_3_out,
       not_4_out, not_5_out, not_6_out, not_7_out, not_8_out, not_9_out, not_10_out, not_11_out, not_12_out,
       or_1_out, or_2_out;
  wire [1:0] controlled_buffer_1_out, REGADDR1;
  wire [7:0] controlled_buffer_4_out, controlled_buffer_8_out, controlled_buffer_13_out,
       controlled_buffer_18_out, controlled_buffer_21_out, controlled_buffer_25_out, REG00OUT0, REG00OUT1,
       REG01OUT0, REG01OUT1, REG10OUT0, REG10OUT1, REG11OUT0, REG11OUT1, REGISTER0_q, REGISTER1_q,
       REGISTER2_q, REGISTER3_q, SUM;

  assign controlled_buffer_1_out = or_1_out ? REGADRR0 : 2'bz;  // Controlled_Buffer controlled_buffer_1
  or or_1 (or_1_out, ADD, or_2_out);
  or or_2 (or_2_out, STR, RDM);
  assign REGADDR1 = ADD ? REGADRR1 : 2'bz;  // Controlled_Buffer controlled_buffer_2
  assign REGADDR1 = not_1_out ? 2'b00 : 2'bz;  // Controlled_Buffer controlled_buffer_3
  not not_1 (not_1_out, ADD);
  and and_1 (and_1_out, and_5_out, RDM);
  assign controlled_buffer_4_out = and_1_out ? RAMOUT : 8'bz;  // Controlled_Buffer controlled_buffer_4
  not not_2 (not_2_out, REGADDR1[0]);
  not not_3 (not_3_out, REGADDR1[1]);
  assign controlled_buffer_1_out = and_2_out ? 2'b00 : 2'bz;  // Controlled_Buffer controlled_buffer_5
  and and_2 (and_2_out, not_4_out, and_3_out);
  not not_4 (not_4_out, ADD);
  and and_3 (and_3_out, not_5_out, not_6_out);
  not not_5 (not_5_out, STR);
  not not_6 (not_6_out, RDM);
  assign REG00OUT0 = and_5_out ? REGISTER0_q : 8'bz;  // Controlled_Buffer controlled_buffer_6
  Register REGISTER0 (.D(controlled_buffer_4_out), .Q(REGISTER0_q), .clk(CLK));  // open: en, clr
  assign REG00OUT1 = and_4_out ? REGISTER0_q : 8'bz;  // Controlled_Buffer controlled_buffer_7
  and and_4 (and_4_out, not_2_out, not_3_out);
  not not_7 (not_7_out, controlled_buffer_1_out[0]);
  not not_8 (not_8_out, controlled_buffer_1_out[1]);
  not not_9 (not_9_out, REGADDR1[1]);
  and and_5 (and_5_out, not_7_out, not_8_out);
  and and_6 (and_6_out, and_8_out, RDM);
  Register REGISTER1 (.D(controlled_buffer_8_out), .Q(REGISTER1_q), .clk(CLK));  // open: en, clr
  assign controlled_buffer_8_out = and_6_out ? RAMOUT : 8'bz;  // Controlled_Buffer controlled_buffer_8
  and and_7 (and_7_out, REGADDR1[0], not_9_out);
  and and_8 (and_8_out, controlled_buffer_1_out[0], not_10_out);
  not not_10 (not_10_out, controlled_buffer_1_out[1]);
  assign REG01OUT0 = and_8_out ? REGISTER1_q : 8'bz;  // Controlled_Buffer controlled_buffer_9
  assign REG01OUT1 = and_7_out ? REGISTER1_q : 8'bz;  // Controlled_Buffer controlled_buffer_10
  assign REGOUT = STR ? REG00OUT0 : 8'bz;  // Controlled_Buffer controlled_buffer_11
  assign REGOUT = STR ? REG01OUT0 : 8'bz;  // Controlled_Buffer controlled_buffer_12
  and and_9 (and_9_out, and_11_out, RDM);
  assign controlled_buffer_13_out = and_9_out ? RAMOUT : 8'bz;  // Controlled_Buffer controlled_buffer_13
  not not_11 (not_11_out, REGADDR1[0]);
  and and_10 (and_10_out, not_11_out, REGADDR1[1]);
  assign REGOUT = STR ? REG10OUT0 : 8'bz;  // Controlled_Buffer controlled_buffer_14
  assign REGOUT = STR ? REG11OUT0 : 8'bz;  // Controlled_Buffer controlled_buffer_15
  not not_12 (not_12_out, controlled_buffer_1_out[0]);
  and and_11 (and_11_out, not_12_out, controlled_buffer_1_out[1]);
  Register REGISTER2 (.D(controlled_buffer_13_out), .Q(REGISTER2_q), .clk(CLK));  // open: en, clr
  assign REG10OUT0 = and_11_out ? REGISTER2_q : 8'bz;  // Controlled_Buffer controlled_buffer_16
  assign REG10OUT1 = and_10_out ? REGISTER2_q : 8'bz;  // Controlled_Buffer controlled_buffer_17
  and and_12 (and_12_out, controlled_buffer_1_out[1], controlled_buffer_1_out[0]);
  and and_13 (and_13_out, and_12_out, RDM);
  Register REGISTER3 (.D(controlled_buffer_18_out), .Q(REGISTER3_q), .clk(CLK));  // open: en, clr
  assign controlled_buffer_18_out = and_13_out ? RAMOUT : 8'bz;  // Controlled_Buffer controlled_buffer_18
  and and_14 (and_14_out, REGADDR1[0], REGADDR1[1]);
  assign REG11OUT0 = and_12_out ? REGISTER3_q : 8'bz;  // Controlled_Buffer controlled_buffer_19
  assign REG11OUT1 = and_14_out ? REGISTER3_q : 8'bz;  // Controlled_Buffer controlled_buffer_20
  assign controlled_buffer_21_out = ADD ? REG00OUT0 : 8'bz;  // Controlled_Buffer controlled_buffer_21
  assign controlled_buffer_21_out = ADD ? REG01OUT0 : 8'bz;  // Controlled_Buffer controlled_buffer_22
  assign controlled_buffer_21_out = ADD ? REG10OUT0 : 8'bz;  // Controlled_Buffer controlled_buffer_23
  assign controlled_buffer_21_out = ADD ? REG11OUT0 : 8'bz;  // Controlled_Buffer controlled_buffer_24
  assign controlled_buffer_25_out = ADD ? REG00OUT1 : 8'bz;  // Controlled_Buffer controlled_buffer_25
  assign controlled_buffer_25_out = ADD ? REG01OUT1 : 8'bz;  // Controlled_Buffer controlled_buffer_26
  assign controlled_buffer_25_out = ADD ? REG10OUT1 : 8'bz;  // Controlled_Buffer controlled_buffer_27
  assign controlled_buffer_25_out = ADD ? REG11OUT1 : 8'bz;  // Controlled_Buffer controlled_buffer_28
  Adder adder_1 (.a(controlled_buffer_21_out), .b(controlled_buffer_25_out), .out(SUM));  // open: cin, cout
  Register ACUMULATOR (.D(SUM), .clk(CLK));  // open: en, Q, clr
endmodule
